# Fritzing sketch esp32_wroom_38_pin_mq135_dht22_ssd1306 (saved by Fritzing 1.0.5)
breadboards: 1

parts:
  A1 = ESP32 38Pin narrow
  Squix1 = OLED 0.96" 128x64 I2C SSD1306
  R1 = Resistor [tolerance=±5% power=0.25W resistance=220 package=THT]

nets:
  N1: A1.Pin_1, Squix1.VCC
  N2: A1.Pin_14, A1.Pin_32, A1.Pin_38, Squix1.GND, R1.Pin_0
  N3: A1.Pin_26, R1.Pin_1
  N4: A1.Pin_33, Squix1.SCA
  N5: A1.Pin_36, Squix1.SCL

custom parts:
  ESP32 38Pin narrow: ESP32 38Pin narrow.
